// Logisim project ImprovedSequentialMultipler.circ as structural Verilog: 1 circuit, main circuit Multiplier
module Multiplier (
  input  [7:0] A,
  input  [7:0] B,
  input  RESET,
  output [15:0] PRODUCT,
  output DONE
);

  wire adder_1_cout, and_1_out, clock_1_out, not_1_out, shift_register_1_out, shift_register_2_out;
  wire [7:0] adder_1_out, multiplexer_1_out;
  wire [7:7] shift_register_1_q0;

  // Probe on A
  Clock clock_1 (.out(clock_1_out));
  Adder adder_1 (
    .a(A), .b({shift_register_1_q0[7], PRODUCT[15:9]}), .out(adder_1_out), .cout(adder_1_cout));  // open: cin
  Shift_Register #(.length(9), .trigger("falling")) shift_register_1 (
    .in(1'b0), .clk(and_1_out), .out(shift_register_1_out), .load(shift_register_2_out), .clr(RESET),
    .d0(adder_1_cout), .q0(shift_register_1_q0[7]), .d1(multiplexer_1_out[7]), .q1(PRODUCT[15]),
    .d2(multiplexer_1_out[6]), .q2(PRODUCT[14]), .d3(multiplexer_1_out[5]), .q3(PRODUCT[13]),
    .d4(multiplexer_1_out[4]), .q4(PRODUCT[12]), .d5(multiplexer_1_out[3]), .q5(PRODUCT[11]),
    .d6(multiplexer_1_out[2]), .q6(PRODUCT[10]), .d7(multiplexer_1_out[1]), .q7(PRODUCT[9]),
    .d8(multiplexer_1_out[0]), .q8(PRODUCT[8]));  // open: shift
  and and_1 (and_1_out, clock_1_out, not_1_out);
  not not_1 (not_1_out, DONE);
  Counter #(.width(4), .max('h9), .ongoal("stay"), .trigger("falling")) counter_1 (
    .D(4'b0000), .count(1'b1), .carry(DONE), .clk(clock_1_out), .clr(RESET));  // open: load, Q
  // Probe on adder_1_out
  Multiplexer #(.width(8), .disabled(0)) multiplexer_1 (
    .in0({shift_register_1_q0[7], PRODUCT[15:9]}), .in1(adder_1_out), .out(multiplexer_1_out),
    .sel(shift_register_2_out), .en(and_1_out));
  Shift_Register #(.trigger("falling")) shift_register_2 (
    .in(shift_register_1_out), .clk(and_1_out), .out(shift_register_2_out), .load(RESET), .d0(B[7]),
    .q0(PRODUCT[7]), .d1(B[6]), .q1(PRODUCT[6]), .d2(B[5]), .q2(PRODUCT[5]), .d3(B[4]), .q3(PRODUCT[4]),
    .d4(B[3]), .q4(PRODUCT[3]), .d5(B[2]), .q5(PRODUCT[2]), .d6(B[1]), .q6(PRODUCT[1]), .d7(B[0]),
    .q7(PRODUCT[0]));  // open: shift, clr
  // Probe on B
  // Probe on PRODUCT

  // Notes on the sheet:
  //   Alexander Chatron-Michaud 260611509
  //   This circuit loads on the falling edge of the clock when the reset button is on. It can then be turned off to begin multiplying
endmodule
